# Fritzing sketch frits_verkeerssimulatie (saved by Fritzing 0.9.3b)
breadboards: 1

parts:
  Part2 = Arduino Uno (Rev3)
  DI1 = 7-Segment LED Display [package=THT]
  R1 = Resistor [tolerance=±5% resistance=220 package="2512 [SMD]"]
  R2 = Resistor [tolerance=±5% resistance=220 package="2512 [SMD]"]
  R3 = Resistor [tolerance=±5% resistance=220 package="2512 [SMD]"]
  R4 = Resistor [tolerance=±5% resistance=220 package="2512 [SMD]"]
  R5 = Resistor [tolerance=±5% resistance=220 package="2512 [SMD]"]
  R6 = Resistor [tolerance=±5% resistance=220 package="2512 [SMD]"]
  R7 = Resistor [tolerance=±5% resistance=220 package="2512 [SMD]"]
  R8 = Resistor [tolerance=±5% resistance=220 package="2512 [SMD]"]
  U1 = 74HC595 [package="DIP16 [THT]"]
  R9 = Rotary Potentiometer (Large) [maximum_resistance=100kΩ package=THT]
  S1 = Pushbutton [package="[THT]"]
  S2 = Pushbutton [package="[THT]"]
  S3 = Pushbutton [package="[THT]"]
  R10 = Resistor [tolerance=±5% resistance=220 package="2512 [SMD]"]
  R11 = Resistor [tolerance=±5% resistance=220 package="2512 [SMD]"]
  R12 = Resistor [tolerance=±5% resistance=220 package="2512 [SMD]"]
  LED1 = smd LED [color="Red (633nm)" package="0603 [SMD]"]
  LED2 = smd LED [color="Yellow (595nm)" package="0603 [SMD]"]
  LED3 = smd LED [color="Green (555nm)" package="0603 [SMD]"]
  LED4 = smd LED [color="Green (555nm)" package="0603 [SMD]"]
  LED5 = smd LED [color="Yellow (595nm)" package="0603 [SMD]"]
  LED6 = smd LED [color="Red (633nm)" package="0603 [SMD]"]
  R13 = Resistor [tolerance=±5% resistance=220 package="2512 [SMD]"]
  R14 = Resistor [tolerance=±5% resistance=220 package="2512 [SMD]"]
  R15 = Resistor [tolerance=±5% resistance=220 package="2512 [SMD]"]
  R16 = Resistor [tolerance=±5% resistance=220 package="2512 [SMD]"]
  R17 = Resistor [tolerance=±5% resistance=220 package="2512 [SMD]"]
  R18 = Resistor [tolerance=±5% resistance=220 package="2512 [SMD]"]
  J1 = Piezo Speaker
  R19 = Resistor [tolerance=±5% resistance=220 package="2512 [SMD]"]
  J2 = Basic Servo
  C1 = Electrolytic Capacitor [capacitance=1µF package="100 mil [THT, electrolytic]"]

nets:
  N1: Part2.A0, R9.wiper
  N2: Part2.A3, S1.Pin_1, S1.Pin_2, R12.Pin_1
  N3: Part2.A4/SDA, S2.Pin_1, S2.Pin_2, R11.Pin_1
  N4: Part2.A5/SCL, S3.Pin_1, S3.Pin_2, R10.Pin_1
  N5: Part2.D8, R19.Pin_1
  N6: Part2.D11_PWM/MOSI, U1.SH_CP
  N7: Part2.D12/MISO, U1.ST_CP
  N8: Part2.D13/SCK, U1.DS
  N9: Part2.D2, LED6.cathode
  N10: Part2.D3_PWM, LED5.cathode
  N11: Part2.D4, LED4.cathode
  N12: Part2.D5_PWM, LED3.cathode
  N13: Part2.D6_PWM, LED2.cathode
  N14: Part2.D7, LED1.cathode
  VCC: Part2.5V, U1.MR, U1.VCC, R9.leg2, S1.Pin_3, S1.Pin_4, S2.Pin_3, S2.Pin_4, S3.Pin_3, S3.Pin_4, J2.vcc, C1.+
  GND: Part2.GND, U1.GND, U1.OE, R9.leg1, R10.Pin_0, R11.Pin_0, R12.Pin_0, R13.Pin_1, R14.Pin_1, R15.Pin_1, R16.Pin_1, R17.Pin_1, R18.Pin_1, J1.pin1, J1.pin2, R19.Pin_0, J2.gnd, C1.-
  N15: DI1.cathodeE, R7.Pin_1
  N16: DI1.cathodeD, R8.Pin_1
  N17: DI1.cathodeC, R1.Pin_0
  N18: DI1.cathodeDP, R6.Pin_0
  N19: DI1.cathodeB, R5.Pin_0
  N20: DI1.cathodeA, R2.Pin_0
  N21: DI1.cathodeF, R3.Pin_1
  N22: DI1.cathodeG, R4.Pin_1
  N23: R1.Pin_1, U1.Q5
  N24: R2.Pin_1, U1.Q6
  N25: R3.Pin_0, U1.Q2
  N26: R4.Pin_0, U1.Q1
  N27: R5.Pin_1, U1.Q7
  N28: R6.Pin_1, U1.Q0
  N29: R7.Pin_0, U1.Q3
  N30: R8.Pin_0, U1.Q4
  N31: LED1.anode, R18.Pin_0
  N32: LED2.anode, R17.Pin_0
  N33: LED3.anode, R16.Pin_0
  N34: LED4.anode, R15.Pin_0
  N35: LED5.anode, R14.Pin_0
  N36: LED6.anode, R13.Pin_0
